// Digital circuit circuito_exp2_ativ2_digital.dig as structural Verilog
module circuito_exp2_ativ2_digital (
  input  zera,
  input  carrega,
  input  conta,
  input  [3:0] chaves,
  input  clock,
  output maior,
  output igual,
  output fim,
  output [3:0] db_contagem,
  output menor
);

  circuito_exp2_ativ2 #(.applicationType("IVERILOG")) u_circuito_exp2_ativ2 (
    .clock(clock), .zera(zera), .carrega(carrega), .conta(conta), .chaves(chaves), .menor(menor),
    .maior(maior), .igual(igual), .fim(fim), .db_contagem(db_contagem));
endmodule

/* Code of circuito_exp2_ativ2:
module circuito_exp2_ativ2 (clock, zera, carrega, conta, chaves, 
                            menor, maior, igual, fim, db_contagem);
    input        clock;
    input        zera;
    input        carrega;
    input        conta;
    input  [3:0] chaves;
    output       menor;
    output       maior;
    output       igual;
    output       fim;
    output [3:0] db_contagem;

    wire   [3:0] s_contagem;  // sinal interno para interligacao dos componentes

    // contador_163
    contador_163 contador (
      .clock( clock ),
      .clr  ( ~zera ),
      .ld   ( ~carrega ),
      .ent  ( 1'b1 ),
      .enp  ( conta ),
      .D    ( chaves ),
      .Q    ( s_contagem ),
      .rco  ( fim )
    );

    // comparador_85
    comparador_85 comparador (
      .A   ( s_contagem ),
      .B   ( chaves ),
      .ALBi( 1'b0 ),
      .AGBi( 1'b0 ),
      .AEBi( 1'b1 ),
      .ALBo( menor ),
      .AGBo( maior ),
      .AEBo( igual )
    );

    // saida de depuracao
    assign db_contagem = s_contagem;
endmodule

module comparador_85 (ALBi, AGBi, AEBi, A, B, ALBo, AGBo, AEBo);

    input[3:0] A, B;
    input      ALBi, AGBi, AEBi;
    output     ALBo, AGBo, AEBo;
    wire[4:0]  CSL, CSG;

    assign CSL  = ~A + B + ALBi;
    assign ALBo = ~CSL[4];
    assign CSG  = A + ~B + AGBi;
    assign AGBo = ~CSG[4];
    assign AEBo = ((A == B) && AEBi);

endmodule

module contador_163 ( clock, clr, ld, ent, enp, D, Q, rco );
    input clock, clr, ld, ent, enp;
    input [3:0] D;
    output reg [3:0] Q;
    output reg rco;

    always @ (posedge clock)
        if (~clr)               Q <= 4'd0;
        else if (~ld)           Q <= D;
        else if (ent && enp)    Q <= Q + 1'b1;
        else                    Q <= Q;
 
    always @ (Q or ent)
        if (ent && (Q == 4'd15))   rco = 1;
        else                       rco = 0;
endmodule
*/
