// Digital circuit circuito_exp2_ativ2_esquematico_digital.dig as structural Verilog
module circuito_exp2_ativ2_esquematico_digital (
  input  ZERA,
  input  CARREGA,
  input  CONTA,
  input  [3:0] DADO,
  input  CLOCK,
  output MENOR,
  output MAIOR,
  output IGUAL,
  output FIM,
  output [3:0] CONTAGEM
);

  wire not_1_out, not_2_out;

  not not_1 (not_1_out, ZERA);
  not not_2 (not_2_out, CARREGA);
  contador_163 #(.applicationType("IVERILOG")) u_contador_163 (
    .CLK(CLOCK), .CLR(not_1_out), .LD(not_2_out), .ENP(1'b1), .ENT(CONTA), .D(DADO), .Q(CONTAGEM), .RCO(FIM));
  comparador_85 #(.applicationType("IVERILOG")) u_comparador_85 (
    .A(CONTAGEM), .B(DADO), .ALBi(1'b0), .AGBi(1'b0), .AEBi(1'b1), .ALBo(MENOR), .AGBo(MAIOR), .AEBo(IGUAL));
endmodule

/* Code of contador_163:
module contador_163 ( CLK, CLR, LD, ENP, ENT, D, Q, RCO );
    input CLK, CLR, LD, ENP, ENT;
    input [3:0] D;
    output reg [3:0] Q;
    output reg RCO;

    always @ (posedge CLK)  // Create the counter f-f behavior
        if (~CLR)               Q <= 4'd0;
        else if (~LD)           Q <= D;
        else if (ENT && ENP)    Q <= Q + 1;
        else                    Q <= Q;
 
    always @ (Q or ENT)     // Create RCO combinational output
        if (ENT && (Q == 4'd15))   RCO = 1;
        else                       RCO = 0;
endmodule
*/

/* Code of comparador_85:
module comparador_85 (ALBi, AGBi, AEBi, A, B, ALBo, AGBo, AEBo);

    input[3:0] A, B;
    input      ALBi, AGBi, AEBi;
    output     ALBo, AGBo, AEBo;
    wire[4:0]  CSL, CSG;

    assign CSL  = ~A + B + ALBi;
    assign ALBo = ~CSL[4];
    assign CSG  = A + ~B + AGBi;
    assign AGBo = ~CSG[4];
    assign AEBo = ((A == B) && AEBi);

endmodule /* comparador_85 * /
*/
